// Digital circuit alu_v2.dig as structural Verilog
module alu_v2 (
  input  [7:0] a_in,
  input  [7:0] b_in,
  input  clk,
  input  [2:0] OPSEL,
  input  rset,
  input  fi,
  input  fc,
  input  fo,
  input  [7:0] bus_in,
  output [7:0] flags_peek,
  output [7:0] sub_peek,
  output [7:0] bus_out
);

  wire comparator_1_eq, comparator_1_gt, comparator_1_lt, opsel_add, opsel_cmp, opsel_sub, or_6_out, or_7_out;
  wire [1:0] add_1_c_o;
  wire [2:2] lookuptable_1_out_2;
  wire [7:0] add_1_s, and_2_out, and_3_out, and_4_out, driver_3_out, driver_6_out, lookuptable_1_out,
       or_3_out, or_4_out, or_5_out, sub_1_c_o;

  Add #(.Bits(8)) add_1 (.a(a_in), .b(b_in), .c_i(1'b0), .s(add_1_s), .c_o(add_1_c_o[0]));
  Sub #(.Bits(8)) sub_1 (.a(a_in), .b(b_in), .c_i(1'b0), .s(sub_peek), .c_o(sub_1_c_o[0]));
  Comparator #(.Bits(8)) comparator_1 (
    .a(a_in), .b(b_in), .gt(comparator_1_gt), .eq(comparator_1_eq), .lt(comparator_1_lt));
  BarrelShifter #(.Bits(8)) barrelshifter_1 (.in(a_in), .shift(4'b0001));  // open: out
  // And and_1 has open pins: In_1=a_in, In_2=b_in, out=open
  // Or or_1 has open pins: In_1=a_in, In_2=b_in, out=open
  // XOr xor_1 has open pins: In_1=a_in, In_2=b_in, out=open
  Decoder #(.Selector_Bits(3)) decoder_1 (
    .sel(OPSEL), .out_1(opsel_add), .out_2(opsel_sub), .out_7(opsel_cmp));  // open: out_0, out_3, out_4, out_5, out_6
  LookUpTable #(.Bits(3)) lookuptable_1 (
    .in0(comparator_1_gt), .in1(comparator_1_eq), .in2(comparator_1_lt),
    .out({lookuptable_1_out_2[2], lookuptable_1_out[1:0]}));
  assign bus_out = opsel_add ? add_1_s : 8'bz;  // Driver driver_1
  Comparator #(.Bits(8)) comparator_2 (.a(add_1_s), .b({8{1'b0}}), .eq(add_1_c_o[1]));  // open: gt, lt
  Comparator #(.Bits(8)) comparator_3 (.a(sub_peek), .b({8{1'b0}}), .eq(sub_1_c_o[1]));  // open: gt, lt
  BitSelector #(.Selector_Bits(3)) bitselector_1 (.in(sub_peek), .sel(3'b111), .out(sub_1_c_o[7]));
  assign and_2_out = flags_peek & 8'h7c;  // And and_2, 8 bits wide
  or or_2 (lookuptable_1_out[7], lookuptable_1_out_2[2], sub_peek[7]);
  assign bus_out = opsel_sub ? sub_peek : 8'bz;  // Driver driver_2
  assign and_3_out = flags_peek & 8'hfc;  // And and_3, 8 bits wide
  assign and_4_out = flags_peek & 8'h3d;  // And and_4, 8 bits wide
  assign or_3_out = and_3_out | {{6{1'b0}}, add_1_c_o};  // Or or_3, 8 bits wide
  assign or_4_out = and_4_out | {sub_1_c_o[7], {5{1'b0}}, sub_1_c_o[1:0]};  // Or or_4, 8 bits wide
  assign or_5_out = and_2_out | {lookuptable_1_out[7], {5{1'b0}}, lookuptable_1_out[1:0]};  // Or or_5, 8 bits wide
  assign driver_3_out = opsel_cmp ? or_5_out : 8'bz;  // Driver driver_3
  assign driver_3_out = opsel_add ? or_3_out : 8'bz;  // Driver driver_4
  assign driver_3_out = opsel_sub ? or_4_out : 8'bz;  // Driver driver_5
  or or_6 (or_6_out, opsel_add, opsel_sub, opsel_cmp);
  assign driver_6_out = or_6_out ? driver_3_out : 8'bz;  // Driver driver_6
  assign driver_6_out = fi ? bus_in : 8'bz;  // Driver driver_7
  or or_7 (or_7_out, fc, rset);
  register FLAGS (
    .bus_in(driver_6_out), .clk(clk), .rfb(or_6_out), .wtb(fo), .rset(or_7_out), .inc(1'b0),
    .bus_out(bus_out), .peek(flags_peek));  // open: cry

  // Notes on the sheet:
  //   Compare Instruction Results
  //   Compare Result	N	Z	C
  //   A, X, or Y < Memory	*	0	0      0b*0000000
  //   A, X, or Y = Memory	0	1	1      0b00000011
  //   A, X, or Y > Memory	*	0	1      0b*0000001
  //   * The N flag will be bit 7 of A, X, or Y - Memory
  //   Flags Register BIts
  //   Carry
  //   Equal/Zero (one flag)
  //   Overflow
  //   negative
  //   7  bit  0
  //   ---- ----
  //   NV1B DIZC
  //   |||| ||||
  //   |||| |||+- Carry
  //   |||| ||+-- Zero
  //   |||| |+--- Interrupt Disable
  //   |||| +---- Decimal
  //   |||+------ (No CPU effect; see: the B flag)
  //   ||+------- (No CPU effect; always pushed as 1)
  //   |+-------- Overflow
  //   +--------- Negative
  //   contents of lookuptable_1 (hex, n*v repeats v):
  //   0,1,3
  //   Addition & Subtraction
  //   FLAGS:
  //   Set overflow if overflow during sub, which is if carry bit is set
  //   Set carry flag if carry is set on addition
endmodule

/* Test case Compare:
clk OPSEL a_in b_in flags_peek sub_peek
# A < B ; A = B ; A > B
C 7 0x00 0xff 0b00000000 X
C 7 0x02 0x02 0b00000011 X
C 7 0x0f 0x00 0b00000001 X

# Tests with negative results
C 7 0x81 0x83 0b10000000 X
C 7 0x81 0x81 0b00000011 X
# THIS TEST NOT WORKING
# C 7 0x8D 0x8F 0b10000011 X
C 7 0x8D 0x8F X X
*/

/* Test case add sub:
clk fc OPSEL a_in b_in flags_peek bus_out
# NV1B DIZC
# Addition Tests
C 0 1 0x00 0xff 0b00000000 0xff
C 0 1 0xff 0x01 0b00000011 0x00
C 0 1 0xff 0x00 0b00000000 0xff

# Subtraction Tests
C 0 2 0x04 0x01 0b00000000 0x03
C 0 2 0x04 0x04 0b00000010 0x00
C 0 2 0x04 0x06 0b10000001 0xFE

# Clear test
C 1 0 0x00 0x00 X Z
# NO-OP test
C 0 0 0x12 0x34 0b00000000 Z
*/
